# Fritzing sketch bridge.v1 (saved by Fritzing 0.9.3b)

parts:
  U1 = FS1000A - 433Mhz RF Transmitter [package=THT]
  Part1 = Adafruit Proto Shield R3 [part_number="Adafruit #2077"]
  U3 = ESP8266 WiFi Module [part_number=ESP8266]
  U4 = XD-RF-5V [package=THT]

nets:
  N1: U1.DATA, Part1.D2
  VCC: U1.VCC, Part1.+5V, U3.3.3V, U4.VCC
  GND: U1.GND, Part1.GND, U3.GND, U4.GND
  N2: Part1.D3, U4.DATA
  N3: Part1.D4, U3.TX
  N4: Part1.D5, U3.RX
  N5: Part1.D7, Part1.LED1

notes:
  ESP01 is connected to a 5 v breakout board

custom parts:
  FS1000A - 433Mhz RF Transmitter: This is 433Mhz RF transmitter with receiver kit for Arduino ARM MCU wireless Application environment: Remote control switch, receiver module, motorcycles, automobile anti-theft products, home security products, electric doors, shutter doors, windows, remote control socket, remote control LED, remote audio remote control electric doors, garage door remote control, remote control retractable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
  Adafruit Proto Shield R3: This prototyping shield is the best out there (well, we think so, at least), and now is even better with Version R3 - updated for the most compatibility with just about all the Arduinos! It works with UNO, Mega, Leonardo, NG, Diecimila, Duemilanove, and compatible Arduinos. Yun's and Arduino Ethernets have a chunky Ethernet jack that gets in the way of stacking, you can use the stacking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
  XD-RF-5V: This is 433Mhz RF transmitter with receiver kit for Arduino ARM MCU wireless Application environment: Remote control switch, receiver module, motorcycles, automobile anti-theft products, home security products, electric doors, shutter doors, windows, remote control socket, remote control LED, remote audio remote control electric doors, garage door remote control, remote control retractable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
